# Fritzing sketch Remote (saved by Fritzing 1.0.6)
circuit board: 10.6386cm x 5.4989cm
breadboards: 1

parts:
  U1 = ESP32-38PinWide [part_number=ESP32-38PinWide]
  S1 = Pushbutton [package="[THT]"]
  R3 = Resistor [tolerance=±5% power=0.25W resistance=10k package=THT]
  S2 = Reed switch [package=THT]
  Q1 = NPN-Transistor [package="TO92 [THT]"]
  S3 = Pushbutton [package=THT]

nets:
  N1: U1.GND, R3.Pin_1, Q1.C, S3.leg1
  N2: U1.VIN, U1.GPIO18, S1.Pin_3, S1.Pin_4, S2.pin_2, Q1.B
  N3: U1.GPIO19, Q1.E
  N4: S1.Pin_1, S1.Pin_2, R3.Pin_0
  N5: S2.pin_1, S3.leg0

custom parts:
  ESP32-38PinWide: Generic 38-Pin ESP32 with wide format (only access to one side of pins on a breadboard) based on Stephen Lilley's HiLetgo ESP-WROOM-32 ESP32 ESP-32S Development Board.
